# Fritzing sketch 111 (saved by Fritzing 0.9.6b)
breadboards: 1

parts:
  M1 = bb-usb-cable [package=THT]  # not connected
  Raspberry_Pi_1 = Raspberry Pi 3 [part_number=RPI-3-V1.2]
  U1 = NodeMCU V1.0  # not connected
  부품4 = FC-28 Soil Hygrometer Module - Probe
  부품5 = FC-28 Soil Hygrometer Module
  S1 = SWITCH-MOMENTARY-2 [package=tactile-pth-12mm]
  S2 = SWITCH-MOMENTARY-2 [package=tactile-pth-12mm]
  KY-2 = Keyes Relay [package=THT]
  KY-3 = Keyes Relay [package=THT]

nets:
  GND: Raspberry_Pi_1.GND, 부품5.GND, KY-2.signal, KY-3.signal
  N1: Raspberry_Pi_1.GPIO5, KY-3.ground
  N2: Raspberry_Pi_1.GPIO6, KY-2.ground
  N3: Raspberry_Pi_1.GPIO13, S2.1
  N4: Raspberry_Pi_1.GPIO19, S1.1
  5V: Raspberry_Pi_1.5V, 부품5.VCC, S1.2, S2.2, KY-2.power, KY-3.power
  N5: 부품4.POS, 부품5.POS
  N6: 부품4.NEG, 부품5.NEG

custom parts:
  bb-usb-cable: Breadboard only, no connectors USB cable for the Raspberry PIs.
  NodeMCU V1.0: ESP8266 based NodeMCU
  FC-28 Soil Hygrometer Module - Probe: The FC-28 is a soil hygrometer module that uses the Texas Instruments LM393 comparator chip to provide an analog measurement of soil humidity.
  FC-28 Soil Hygrometer Module: The FC-28 is a soil hygrometer module that uses the Texas Instruments LM393 comparator chip to provide an analog measurement of soil humidity. The digital output is high when soil moisture is over a certain threshold, as determined by adjusting the potentiometer.
  Keyes Relay: The Keyes 5V relay module is suitable for SCM development, home appliance control. It uses a 5V~12V TIL control signal which can control DC / AC signal.
